// Digital circuit ExamenII_Orga.dig as structural Verilog
module ExamenII_Orga (
  input  [31:0] addr,
  output [31:0] data,
  output hit
);

  wire [1:0] valid;
  wire [29:20] rom_1_d;

  ROM #(.AddrBits(10), .Bits(32)) rom_1 (.A(addr[11:2]), .sel(1'b1), .D({valid, rom_1_d, data[19:0]}));
  Comparator comparator_1 (.a(rom_1_d[20]), .b(addr[12]), .eq(hit));  // open: gt, lt
  // Pins of 1 and 10 bits meet at rom_1_d
  // Pins of 1 and 20 bits meet at addr[31:12]
  // Pins of 20 and 32 bits meet at data

  // Other names for the same wires on the sheet: byte_offset[1:0] = addr[1:0]; index[9:0] = addr[11:2];
  //   tag[19:0] = addr[31:12]

  // Notes on the sheet:
  //   Memoria Caché
endmodule
